# Fritzing sketch 140402 Firefly PhoneHome v9 (saved by Fritzing 0.8.7b)
circuit board: 23.1804cm x 12.3083cm

parts:
  Part2 = Arduino Uno (Rev3)
  JACK1 = 2.1mm Barrel Jack with Terminal Block
  BMP1 = BMP085 Breakout
  VCC1 = Battery block 9V
  VCC2 = Battery block 9V
  DFRobot_LCD_keypad_shield1 = LCD keypad Shield
  Part3 = Arduino Cellular Shield
  LED4 = LED - 5mm [color="Blue (470nm)" package="5 mm [THT]"]
  LED5 = LED - 5mm [color="Blue (470nm)" package="5 mm [THT]"]
  LED6 = LED - 5mm [color="Blue (470nm)" package="5 mm [THT]"]

nets:
  N1: Part2.A4/SDA, BMP1.SDA, DFRobot_LCD_keypad_shield1.RX
  N2: Part2.A5/SCL, BMP1.SCL, DFRobot_LCD_keypad_shield1.TX
  N3: Part2.D12/MISO, LED4.anode, LED5.anode, LED6.anode
  GND: Part2.GND, DFRobot_LCD_keypad_shield1.GND, LED4.cathode, LED5.cathode, LED6.cathode
  5V: Part2.5V, BMP1.VIN
  VIN: Part2.VIN, DFRobot_LCD_keypad_shield1.VCC
  N4: JACK1.POS, VCC1.+
  N5: JACK1.NEG, VCC1.-
  N6: VCC2.-, Part3.GND
  N7: VCC2.+, Part3.VRAW

custom parts:
  BMP085 Breakout: A breakout for the BMP085 barometric pressure and temperature sensor
  LCD keypad Shield: A 2 row LCD shield with buttons, and contrast regulator.
