# Fritzing sketch 140303 Firefly PhoneHome v2 (saved by Fritzing 0.8.7b)
circuit board: 18.1908cm x 10.0276cm
breadboards: 1

parts:
  Part1 = Electric Imp April
  BATT2 = 4xAA Switchable Battery Pack w/Bare Wire
  Part2 = Arduino Uno (Rev3)
  JACK1 = 2.1mm Barrel Jack with Terminal Block
  BMP1 = BMP085 Breakout
  S1 = Pushbutton [package="[THT]"]
  R2 = Resistor [tolerance=±5% resistance=10k package="0603 [SMD]"]

nets:
  N1: Part1.4, Part2.D1/TX
  3V3: Part1.10, Part2.3V3, BMP1.VIN, S1.Pin_3, S1.Pin_4
  N2: BATT2.POS, JACK1.POS
  N3: BATT2.NEG, JACK1.NEG
  N4: Part2.A4/SDA, BMP1.SDA
  N5: Part2.A5/SCL, BMP1.SCL
  GND: Part2.GND, BMP1.GND, R2.Pin_1
  N6: S1.Pin_1, S1.Pin_2, R2.Pin_0

custom parts:
  Electric Imp April: Electric Imp Breakout Board with onboard 3.3V regulated power supply
  4xAA Switchable Battery Pack w/Bare Wire: 4xAA Switchable Battery Pack with Bare Wire connection
  BMP085 Breakout: A breakout for the BMP085 barometric pressure and temperature sensor
