# Fritzing sketch 140303 Firefly PhoneHome v3 (saved by Fritzing 0.8.7b)
circuit board: 18.1908cm x 10.0276cm
breadboards: 1

parts:
  Part1 = Electric Imp April
  BATT2 = 4xAA Switchable Battery Pack w/Bare Wire
  Part2 = Arduino Uno (Rev3)
  JACK1 = 2.1mm Barrel Jack with Terminal Block
  BMP1 = BMP085 Breakout
  D1 = Diode [package=diode-1n4148]
  R2 = Resistor [tolerance=±5% resistance=10k package="0603 [SMD]"]
  S1 = Pushbutton [package="[THT]"]
  R3 = Resistor [tolerance=±5% resistance=1k package=THT]
  BATT3 = 4xAA Switchable Battery Pack w/Bare Wire  # not connected

nets:
  N1: Part1.1, D1.A
  N2: Part1.4, Part2.D1/TX
  N3: Part1.7, Part1.10, Part2.3V3, S1.Pin_3, S1.Pin_4, R3.Pin_0
  N4: Part1.9, R2.Pin_1
  N5: BATT2.POS, JACK1.POS
  N6: BATT2.NEG, JACK1.NEG
  N7: Part2.A4/SDA, BMP1.SDA
  N8: Part2.A5/SCL, BMP1.SCL
  GND: Part2.GND, BMP1.GND
  N9: BMP1.VIN, R3.Pin_1
  N10: R2.Pin_0, S1.Pin_1, S1.Pin_2

notes:
  Read led state:
  This is connected to the red light wire on the Firefly led board
  This is connected to ground on firefly
  Turn on/off light:
  This is connected to the Red Light wire on the firefly led board
  Connect to C+ and C- on firefly led display boad to increase the brightness of the leds

custom parts:
  Electric Imp April: Electric Imp Breakout Board with onboard 3.3V regulated power supply
  4xAA Switchable Battery Pack w/Bare Wire: 4xAA Switchable Battery Pack with Bare Wire connection
  BMP085 Breakout: A breakout for the BMP085 barometric pressure and temperature sensor
