# Fritzing sketch 140303 Firefly PhoneHome v5 (saved by Fritzing 0.8.7b)
circuit board: 18.1908cm x 10.0276cm
breadboards: 1

parts:
  Part1 = Electric Imp April
  Part2 = Arduino Uno (Rev3)
  JACK1 = 2.1mm Barrel Jack with Terminal Block
  BMP1 = BMP085 Breakout
  S1 = Pushbutton [package="[THT]"]
  VCC1 = Battery block 9V
  LED1 = RGB LED (com. anode, rbg) [package="5 mm [THT]"]
  LED2 = RGB LED (com. cathode, rgb) [package="5 mm [THT]"]
  LED3 = RGB LED (com. cathode, rgb) [package="5 mm [THT]"]
  VCC2 = Battery block 9V
  R2 = Resistor [tolerance=±5% resistance=10k package="0603 [SMD]"]

nets:
  N1: Part1.1, Part2.D8, Part2.3V3, S1.Pin_3, S1.Pin_4
  N2: Part1.4, Part2.D1/TX
  N3: Part1.8, BMP1.VIN
  N4: Part1.9, BMP1.GND
  N5: Part1.10, VCC2.+
  N6: Part1.11, VCC2.-
  N7: Part2.A4/SDA, BMP1.SDA
  N8: Part2.A5/SCL, BMP1.SCL
  N9: Part2.D12/MISO, LED1.green_cathode, LED2.blue_anode, LED3.blue_anode
  N10: Part2.GND, LED1.common_anode, LED2.common_cathode, LED3.common_cathode, R2.Pin_1
  N11: JACK1.POS, VCC1.+
  N12: JACK1.NEG, VCC1.-
  N13: S1.Pin_1, S1.Pin_2, R2.Pin_0

custom parts:
  Electric Imp April: Electric Imp Breakout Board with onboard 3.3V regulated power supply
  BMP085 Breakout: A breakout for the BMP085 barometric pressure and temperature sensor
