# Fritzing sketch 140313 Firefly PhoneHome v7 (saved by Fritzing 0.8.7b)
circuit board: 18.1908cm x 10.0276cm

parts:
  Part1 = Electric Imp April
  Part2 = Arduino Uno (Rev3)
  JACK1 = 2.1mm Barrel Jack with Terminal Block
  BMP1 = BMP085 Breakout
  VCC1 = Battery block 9V
  LED1 = RGB LED (com. anode, rbg) [package="5 mm [THT]"]
  LED2 = RGB LED (com. cathode, rgb) [package="5 mm [THT]"]
  LED3 = RGB LED (com. cathode, rgb) [package="5 mm [THT]"]
  VCC2 = Battery block 9V

nets:
  N1: Part1.1, Part2.D7
  N2: Part1.4, Part2.D1/TX
  N3: Part1.9, BMP1.GND
  N4: Part1.10, VCC2.+
  N5: Part1.11, VCC2.-
  N6: Part2.A4/SDA, BMP1.SDA
  N7: Part2.A5/SCL, BMP1.SCL
  N8: Part2.D12/MISO, LED1.green_cathode, LED2.blue_anode, LED3.blue_anode
  N9: Part2.GND, LED1.common_anode, LED2.common_cathode, LED3.common_cathode
  5V: Part2.5V, BMP1.VIN
  N10: JACK1.POS, VCC1.+
  N11: JACK1.NEG, VCC1.-

custom parts:
  Electric Imp April: Electric Imp Breakout Board with onboard 3.3V regulated power supply
  BMP085 Breakout: A breakout for the BMP085 barometric pressure and temperature sensor
