# Fritzing sketch 140330 Firefly PhoneHome v8 (saved by Fritzing 0.8.7b)
circuit board: 18.1908cm x 10.0276cm

parts:
  Part1 = Electric Imp April
  Part2 = Arduino Uno (Rev3)
  JACK1 = 2.1mm Barrel Jack with Terminal Block
  BMP1 = BMP085 Breakout
  VCC1 = Battery block 9V
  LED1 = RGB LED (com. anode, rbg) [package="5 mm [THT]"]
  LED2 = RGB LED (com. cathode, rgb) [package="5 mm [THT]"]
  LED3 = RGB LED (com. cathode, rgb) [package="5 mm [THT]"]
  VCC2 = Battery block 9V
  DFRobot_LCD_keypad_shield1 = LCD keypad Shield

nets (from the pcb view):
  N1: Part1.1, Part2.D7
  N2: Part1.4, Part2.D1/TX
  N3: Part1.9, BMP1.GND
  N4: Part1.10, VCC2.+
  N5: Part1.11, VCC2.-
  N6: Part2.A4/SDA, BMP1.SDA, DFRobot_LCD_keypad_shield1.RX
  N7: Part2.A5/SCL, BMP1.SCL, DFRobot_LCD_keypad_shield1.TX
  N8: Part2.D12/MISO, LED1.green_cathode, LED2.blue_anode, LED3.blue_anode
  GND: Part2.GND, LED1.common_anode, LED2.common_cathode, LED3.common_cathode, DFRobot_LCD_keypad_shield1.GND
  5V: Part2.5V, BMP1.VIN
  VIN: Part2.VIN, DFRobot_LCD_keypad_shield1.VCC
  N9: JACK1.POS, VCC1.+
  N10: JACK1.NEG, VCC1.-

custom parts:
  Electric Imp April: Electric Imp Breakout Board with onboard 3.3V regulated power supply
  BMP085 Breakout: A breakout for the BMP085 barometric pressure and temperature sensor
  LCD keypad Shield: A 2 row LCD shield with buttons, and contrast regulator.
